# Fritzing sketch Schematics (saved by Fritzing 0.9.3b)
breadboards: 1

parts:
  R1 = Resistor [tolerance=±5% resistance=1k package=THT]
  R2 = Resistor [tolerance=±5% resistance=1k package=THT]
  Raspberry_Pi_1 = Raspberry Pi 3 [part_number=RPI-3-V1.2]
  Composant1 = Lithium Ion Cylindrical Battery 3.7v 2200mAh [part_number=1781]
  Composant2 = Lithium Ion Cylindrical Battery 3.7v 2200mAh [part_number=1781]
  Composant3 = Lithium Ion Cylindrical Battery 3.7v 2200mAh [part_number=1781]
  Composant4 = Lithium Ion Cylindrical Battery 3.7v 2200mAh [part_number=1781]
  Composant5 = Lithium Ion Cylindrical Battery 3.7v 2200mAh [part_number=1781]
  Composant6 = Lithium Ion Cylindrical Battery 3.7v 2200mAh [part_number=1781]
  Composant7 = Lithium Ion Cylindrical Battery 3.7v 2200mAh [part_number=1781]
  Composant8 = Lithium Ion Cylindrical Battery 3.7v 2200mAh [part_number=1781]
  Composant9 = Lithium Ion Cylindrical Battery 3.7v 2200mAh [part_number=1781]
  Composant10 = Lithium Ion Cylindrical Battery 3.7v 2200mAh [part_number=1781]
  IC1 = MCP3008 8-channel 10-bit ADC [part_number=MCP3008]
  IC2 = MCP3008 8-channel 10-bit ADC [part_number=MCP3008]
  R3 = Resistor [tolerance=±5% resistance=10k package=THT]
  R4 = Resistor [tolerance=±5% resistance=10k package=THT]
  R5 = Resistor [tolerance=±5% resistance=10k package=THT]
  R6 = Resistor [tolerance=±5% resistance=10k package=THT]
  R7 = Resistor [tolerance=±5% resistance=10k package=THT]
  R8 = Resistor [tolerance=±5% resistance=10k package=THT]
  R9 = Resistor [tolerance=±5% resistance=10k package=THT]
  R10 = Resistor [tolerance=±5% resistance=10k package=THT]
  R11 = Resistor [tolerance=±5% resistance=1k package=THT]
  R12 = Resistor [tolerance=±5% resistance=1k package=THT]
  R13 = Resistor [tolerance=±5% resistance=1k package=THT]
  R14 = Resistor [tolerance=±5% resistance=1k package=THT]
  R15 = Resistor [tolerance=±5% resistance=1k package=THT]
  R16 = Resistor [tolerance=±5% resistance=1k package=THT]
  R17 = Resistor [tolerance=±5% resistance=1k package=THT]
  R18 = Resistor [tolerance=±5% resistance=1k package=THT]

nets:
  N1: R1.Pin_0, Composant8.positive, Composant9.negative
  N2: R1.Pin_1, R2.Pin_0, IC2.no_name_yet#2
  N3: R2.Pin_1, Composant7.negative, R11.Pin_1, R12.Pin_1, R13.Pin_1, R14.Pin_1, R15.Pin_1, R16.Pin_1, R17.Pin_1, R18.Pin_1
  N4: Raspberry_Pi_1.GPIO10, Raspberry_Pi_1.GND, IC1.no_name_yet#9, IC1.no_name_yet#11, IC1.no_name_yet#14, IC2.no_name_yet#9, IC2.no_name_yet#11, IC2.no_name_yet#14
  N5: Raspberry_Pi_1.GPIO9, Raspberry_Pi_1.GPIO25, IC1.no_name_yet#12, IC2.no_name_yet#12
  N6: Raspberry_Pi_1.GPIO11, IC1.no_name_yet#13, IC2.no_name_yet#13
  N7: Raspberry_Pi_1.GPIO7, IC1.no_name_yet#10
  N8: Raspberry_Pi_1.GPIO8, IC2.no_name_yet#10
  N9: Raspberry_Pi_1.5V, IC1.no_name_yet#15, IC1.no_name_yet#16, IC2.no_name_yet#15, IC2.no_name_yet#16
  N10: Composant1.positive, R10.Pin_0
  N11: Composant1.negative, Composant2.positive, R9.Pin_0
  N12: Composant2.negative, Composant3.positive, R8.Pin_0
  N13: Composant3.negative, Composant4.positive, R7.Pin_0
  N14: Composant4.negative, Composant5.positive, R6.Pin_0
  N15: Composant5.negative, Composant6.positive, R5.Pin_0
  N16: Composant6.negative, Composant10.positive, R4.Pin_0
  N17: Composant7.positive, Composant8.negative, IC2.no_name_yet#1
  N18: Composant9.positive, Composant10.negative, R3.Pin_0
  N19: IC1.no_name_yet#1, R9.Pin_1, R17.Pin_0
  N20: IC1.no_name_yet#2, R10.Pin_1, R18.Pin_0
  N21: IC2.no_name_yet#3, R3.Pin_1, R11.Pin_0
  N22: IC2.no_name_yet#4, R4.Pin_1, R12.Pin_0
  N23: IC2.no_name_yet#5, R5.Pin_1, R13.Pin_0
  N24: IC2.no_name_yet#6, R6.Pin_1, R14.Pin_0
  N25: IC2.no_name_yet#7, R7.Pin_1, R15.Pin_0
  N26: IC2.no_name_yet#8, R8.Pin_1, R16.Pin_0

notes:
  l'impédance d'entrée du MCP3008 fait en sorte qu'il ne faut pas mettre de résistances supérieures à 10kOhm dans le pont diviseur de tension, sous peine de fausser les mesures

custom parts:
  Lithium Ion Cylindrical Battery 3.7v 2200mAh: This lithium ion battery has a capacity of 2200mAh and a protection circuit that provides over-voltage, under-voltage and over-current protection. This cell can provide 2C of peak current (4400mA). Note that these batteries are not designed to sustain such high loads, we suggest keeping any constant current draw under about 0.5C (1 Amp).
